# Fritzing sketch p1_connector-opencollector (saved by Fritzing 0.9.3b)
circuit board: 8.46667cm x 5.64444cm
breadboards: 1

parts:
  NPN_(2N2222A) = NPN-Transistor [package="TO92 [THT]"]
  R1 = Resistor [tolerance=±5% resistance=10k package=THT]
  Raspberry_Pi_Zero1 = Raspberry Pi Zero
  R2 = Resistor [tolerance=±5% resistance=100k package=THT]
  P1 = RJ11 Jack [package=rj11-6]
  U2 = Voltage Regulator - 5V [package="DPak [SMD]"]

nets:
  GND: NPN_(2N2222A).E, Raspberry_Pi_Zero1.GND, P1.6, U2.GND
  N1: NPN_(2N2222A).B, R2.Pin_1
  N2: NPN_(2N2222A).C, R1.Pin_1, Raspberry_Pi_Zero1.GIPO15
  N3: R1.Pin_0, R2.Pin_0, P1.3, U2.output_voltage
  N4: Raspberry_Pi_Zero1.5V, P1.1, U2.input_voltage

notes:
  P1 TX (5V)
  P1 5V/GND
  5V/GND
  RX (3V)
  RX
  P1 TX
  TX
  GRD
  Request
