# Fritzing sketch p1_connector-v2 (saved by Fritzing 0.9.3b)
circuit board: 8.46667cm x 5.64444cm
breadboards: 1

parts:
  NPN_(2N2222A) = NPN-Transistor [package="TO92 [THT]"]
  R4 = Resistor [tolerance=±5% resistance=10k package=THT]
  Raspberry_Pi_Zero1 = Raspberry Pi Zero
  R5 = Resistor [tolerance=±5% resistance=100k package=THT]
  P1 = RJ11 Jack [package=rj11-6]
  U1 = Voltage Regulator - 5V [package="DPak [SMD]"]

nets:
  GND: NPN_(2N2222A).E, Raspberry_Pi_Zero1.GND, P1.6, U1.GND
  N1: NPN_(2N2222A).B, R5.Pin_1
  N2: NPN_(2N2222A).C, R4.Pin_1, Raspberry_Pi_Zero1.GIPO15
  N3: R4.Pin_0, U1.output_voltage
  N4: Raspberry_Pi_Zero1.5V, P1.1, U1.input_voltage
  N5: R5.Pin_0, P1.3

notes:
  P1 TX (5V)
  P1 5V/GND
  5V/GND
  RX (3V)
  RX
  P1 TX
  TX
  GRD
  Request
