# Fritzing sketch p1_connector-voltagedivider (saved by Fritzing 0.9.3b)
circuit board: 8.46667cm x 5.64444cm
breadboards: 1

parts:
  R2 = Resistor [tolerance=±5% resistance=10k package=THT]
  R3 = Resistor [tolerance=±5% resistance=4.7k package=THT]
  Q1 = NPN-Transistor [package="TO92 [THT]"]
  R1 = Resistor [tolerance=±5% resistance=100k package=THT]
  R4 = Resistor [tolerance=±5% resistance=10k package=THT]

nets:
  N1: R2.Pin_0, R3.Pin_1, R4.Pin_0
  GND: R2.Pin_1, Q1.E
  5V: R3.Pin_0
  N2: Q1.B, R1.Pin_0, R1.Pin_1
  N3: Q1.C, R4.Pin_1

notes:
  P1 TX (5V)
  P1 5V/GND
  5V/GND
  RX (3V)
  RX
  P1 TX
